// Logisim project Lab3.circ as structural Verilog: 7 circuits, main circuit main
module main (
  input  [31:0] Instruction
);

  wire alu_control_1_alu_src, clock_1_out;
  wire [3:0] alu_control_1_alu_ctrl0;
  wire [31:0] alu32_1_result, bit_extender_1_out, multiplexer_1_out, register_32_bit_1_rdata1,
       register_32_bit_1_rdata2;

  Clock clock_1 (.out(clock_1_out));
  assign bit_extender_1_out = {{20{Instruction[31]}}, Instruction[31:20]};  // Bit_Extender bit_extender_1
  Register_32_bit register_32_bit_1 (
    .RReg1(Instruction[19:15]), .WData(alu32_1_result), .Clock_in(clock_1_out), .RReg2(Instruction[24:20]),
    .Write(1'b1), .WReg(Instruction[11:7]), .RData1(register_32_bit_1_rdata1),
    .RData2(register_32_bit_1_rdata2));
  ALU_Control alu_control_1 (
    .I30(Instruction[30]), .I14(Instruction[14]), .I13(Instruction[13]), .I12(Instruction[12]),
    .I6(Instruction[6]), .I5(Instruction[5]), .I4(Instruction[4]), .ALU_Ctrl3(alu_control_1_alu_ctrl0[3]),
    .ALU_Ctrl2(alu_control_1_alu_ctrl0[2]), .ALU_Ctrl1(alu_control_1_alu_ctrl0[1]),
    .ALU_Ctrl0(alu_control_1_alu_ctrl0[0]), .ALU_Src(alu_control_1_alu_src));
  Multiplexer #(.enable("false"), .width(32)) multiplexer_1 (
    .in0(register_32_bit_1_rdata2), .in1(bit_extender_1_out), .out(multiplexer_1_out),
    .sel(alu_control_1_alu_src));
  ALU32 alu32_1 (
    .ALU_Ctrl(alu_control_1_alu_ctrl0), .A(register_32_bit_1_rdata1), .B(multiplexer_1_out),
    .Result(alu32_1_result));
endmodule

module ALU_Control (
  input  I30,
  input  I14,
  input  I13,
  input  I12,
  input  I6,
  input  I5,
  input  I4,
  output ALU_Ctrl3,
  output ALU_Ctrl2,
  output ALU_Ctrl1,
  output ALU_Ctrl0,
  output ALU_Src
);

  wire and_2_out, and_3_out, not_1_out, not_2_out, not_3_out, not_4_out, not_5_out;

  not not_1 (not_1_out, I14);
  not not_2 (not_2_out, I13);
  not not_3 (not_3_out, I12);
  not not_4 (not_4_out, I5);
  not not_5 (not_5_out, I4);
  and and_1 (ALU_Ctrl2, I30, not_2_out, I5);
  and and_2 (and_2_out, not_1_out, not_4_out);
  and and_3 (and_3_out, I13, not_3_out);
  or or_1 (ALU_Src, not_4_out, not_5_out);
  or or_2 (ALU_Ctrl1, and_2_out, not_2_out);
  or or_3 (ALU_Ctrl0, not_1_out, and_3_out);

  assign ALU_Ctrl3 = 1'b0;
endmodule

module one_bit_full_adder (
  input  A,
  input  B,
  input  C_in,
  output S,
  output C_out
);

  wire and_1_out, and_2_out, and_3_out, and_4_out, and_5_out, and_6_out, nand_1_out;

  and and_1 (and_1_out, A, B);
  and and_2 (and_2_out, A, B);
  and and_3 (and_3_out, A, B, C_in);
  and and_4 (and_4_out, A, B, C_in);
  and and_5 (and_5_out, and_1_out, C_in);
  and and_6 (and_6_out, nand_1_out, and_3_out);
  nand nand_1 (nand_1_out, and_5_out, and_2_out);
  and and_7 (C_out, and_6_out, and_4_out);
  not not_1 (S, nand_1_out);
endmodule

module one_bit_ALU (
  input  [3:0] ALU_Ctrl,
  input  A,
  input  B,
  input  C_in,
  output R,
  output C_out
);

  wire and_1_out, multiplexer_1_out, not_1_out, one_bit_full_adder_1_s, or_1_out, xor_1_out;

  not not_1 (not_1_out, B);
  Multiplexer #(.enable("false")) multiplexer_1 (.in0(B), .in1(not_1_out), .out(multiplexer_1_out), .sel(ALU_Ctrl[2]));
  and and_1 (and_1_out, A, multiplexer_1_out);
  or or_1 (or_1_out, A, multiplexer_1_out);
  xor xor_1 (xor_1_out, A, multiplexer_1_out);
  one_bit_full_adder one_bit_full_adder_1 (
    .A(A), .B(multiplexer_1_out), .C_in(C_in), .S(one_bit_full_adder_1_s), .C_out(C_out));
  Multiplexer #(.enable("false"), .select(2)) multiplexer_2 (
    .in0(and_1_out), .in1(or_1_out), .in2(xor_1_out), .in3(one_bit_full_adder_1_s), .out(R),
    .sel(ALU_Ctrl[1:0]));
endmodule

module ALU4 (
  input  [3:0] ALU_Ctrl,
  input  [3:0] A,
  input  [3:0] B,
  input  C_in,
  output [3:0] R,
  output C_out
);

  wire one_bit_alu_1_c_out, one_bit_alu_2_c_out, one_bit_alu_3_c_out;

  one_bit_ALU one_bit_alu_1 (
    .ALU_Ctrl(ALU_Ctrl), .A(A[0]), .B(B[0]), .C_in(C_in), .R(R[0]), .C_out(one_bit_alu_1_c_out));
  one_bit_ALU one_bit_alu_2 (
    .ALU_Ctrl(ALU_Ctrl), .A(A[1]), .B(B[1]), .C_in(one_bit_alu_1_c_out), .R(R[1]), .C_out(one_bit_alu_2_c_out));
  one_bit_ALU one_bit_alu_3 (
    .ALU_Ctrl(ALU_Ctrl), .A(A[2]), .B(B[2]), .C_in(one_bit_alu_2_c_out), .R(R[2]), .C_out(one_bit_alu_3_c_out));
  one_bit_ALU one_bit_alu_4 (
    .ALU_Ctrl(ALU_Ctrl), .A(A[3]), .B(B[3]), .C_in(one_bit_alu_3_c_out), .R(R[3]), .C_out(C_out));
endmodule

module ALU32 (
  input  [3:0] ALU_Ctrl,
  input  [31:0] A,
  input  [31:0] B,
  output [31:0] Result
);

  wire alu4_1_c_out, alu4_2_c_out, alu4_3_c_out, alu4_4_c_out, alu4_5_c_out, alu4_6_c_out, alu4_7_c_out;

  ALU4 alu4_1 (
    .ALU_Ctrl({ALU_Ctrl[2], ALU_Ctrl[3], ALU_Ctrl[1:0]}), .A(A[3:0]), .B(B[3:0]), .C_in(ALU_Ctrl[3]),
    .R(Result[3:0]), .C_out(alu4_1_c_out));
  ALU4 alu4_2 (
    .ALU_Ctrl({ALU_Ctrl[2], ALU_Ctrl[3], ALU_Ctrl[1:0]}), .A(A[7:4]), .B(B[7:4]), .C_in(alu4_1_c_out),
    .R(Result[7:4]), .C_out(alu4_2_c_out));
  ALU4 alu4_3 (
    .ALU_Ctrl({ALU_Ctrl[2], ALU_Ctrl[3], ALU_Ctrl[1:0]}), .A(A[11:8]), .B(B[11:8]), .C_in(alu4_2_c_out),
    .R(Result[11:8]), .C_out(alu4_3_c_out));
  ALU4 alu4_4 (
    .ALU_Ctrl({ALU_Ctrl[2], ALU_Ctrl[3], ALU_Ctrl[1:0]}), .A(A[15:12]), .B(B[15:12]), .C_in(alu4_3_c_out),
    .R(Result[15:12]), .C_out(alu4_4_c_out));
  ALU4 alu4_5 (
    .ALU_Ctrl({ALU_Ctrl[2], ALU_Ctrl[3], ALU_Ctrl[1:0]}), .A(A[19:16]), .B(B[19:16]), .C_in(alu4_4_c_out),
    .R(Result[19:16]), .C_out(alu4_5_c_out));
  ALU4 alu4_6 (
    .ALU_Ctrl({ALU_Ctrl[2], ALU_Ctrl[3], ALU_Ctrl[1:0]}), .A(A[23:20]), .B(B[23:20]), .C_in(alu4_5_c_out),
    .R(Result[23:20]), .C_out(alu4_6_c_out));
  ALU4 alu4_7 (
    .ALU_Ctrl({ALU_Ctrl[2], ALU_Ctrl[3], ALU_Ctrl[1:0]}), .A(A[27:24]), .B(B[27:24]), .C_in(alu4_6_c_out),
    .R(Result[27:24]), .C_out(alu4_7_c_out));
  ALU4 alu4_8 (
    .ALU_Ctrl({ALU_Ctrl[2], ALU_Ctrl[3], ALU_Ctrl[1:0]}), .A(A[31:28]), .B(B[31:28]), .C_in(alu4_7_c_out),
    .R(Result[31:28]));  // open: C_out
endmodule

module Register_32_bit (
  input  [4:0] RReg1,
  input  [31:0] WData,
  input  Clock_in,
  input  [4:0] RReg2,
  input  Write,
  input  [4:0] WReg,
  output [31:0] RData1,
  output [31:0] RData2
);

  wire demultiplexer_1_out0, demultiplexer_1_out1, demultiplexer_1_out2, demultiplexer_1_out3,
       demultiplexer_1_out4, demultiplexer_1_out5, demultiplexer_1_out6, demultiplexer_1_out7,
       demultiplexer_1_out8, demultiplexer_1_out9, demultiplexer_1_out10, demultiplexer_1_out11,
       demultiplexer_1_out12, demultiplexer_1_out13, demultiplexer_1_out14, demultiplexer_1_out15,
       demultiplexer_1_out16, demultiplexer_1_out17, demultiplexer_1_out18, demultiplexer_1_out19,
       demultiplexer_1_out20, demultiplexer_1_out21, demultiplexer_1_out22, demultiplexer_1_out23,
       demultiplexer_1_out24, demultiplexer_1_out25, demultiplexer_1_out26, demultiplexer_1_out27,
       demultiplexer_1_out28, demultiplexer_1_out29, demultiplexer_1_out30, demultiplexer_1_out31;
  wire [31:0] register_1_q, register_2_q, register_3_q, register_4_q, register_5_q, register_6_q,
       register_7_q, register_8_q, register_9_q, register_10_q, register_11_q, register_12_q, register_13_q,
       register_14_q, register_15_q, register_16_q, register_17_q, register_18_q, register_19_q,
       register_20_q, register_21_q, register_22_q, register_23_q, register_24_q, register_25_q,
       register_26_q, register_27_q, register_28_q, register_29_q, register_30_q, register_31_q,
       register_32_q;

  Demultiplexer #(.enable("false"), .select(5)) demultiplexer_1 (
    .out0(demultiplexer_1_out0), .out1(demultiplexer_1_out1), .out2(demultiplexer_1_out2),
    .out3(demultiplexer_1_out3), .out4(demultiplexer_1_out4), .out5(demultiplexer_1_out5),
    .out6(demultiplexer_1_out6), .out7(demultiplexer_1_out7), .out8(demultiplexer_1_out8),
    .out9(demultiplexer_1_out9), .out10(demultiplexer_1_out10), .out11(demultiplexer_1_out11),
    .out12(demultiplexer_1_out12), .out13(demultiplexer_1_out13), .out14(demultiplexer_1_out14),
    .out15(demultiplexer_1_out15), .out16(demultiplexer_1_out16), .out17(demultiplexer_1_out17),
    .out18(demultiplexer_1_out18), .out19(demultiplexer_1_out19), .out20(demultiplexer_1_out20),
    .out21(demultiplexer_1_out21), .out22(demultiplexer_1_out22), .out23(demultiplexer_1_out23),
    .out24(demultiplexer_1_out24), .out25(demultiplexer_1_out25), .out26(demultiplexer_1_out26),
    .out27(demultiplexer_1_out27), .out28(demultiplexer_1_out28), .out29(demultiplexer_1_out29),
    .out30(demultiplexer_1_out30), .out31(demultiplexer_1_out31), .in(Write), .sel(WReg));
  Register #(.width(32)) register_1 (
    .D(WData), .en(demultiplexer_1_out0), .clk(Clock_in), .Q(register_1_q), .clr(Write));
  Register #(.width(32)) register_2 (
    .D(WData), .en(demultiplexer_1_out1), .clk(Clock_in), .Q(register_2_q));  // open: clr
  Register #(.width(32)) register_3 (
    .D(WData), .en(demultiplexer_1_out2), .clk(Clock_in), .Q(register_3_q));  // open: clr
  Register #(.width(32)) register_4 (
    .D(WData), .en(demultiplexer_1_out3), .clk(Clock_in), .Q(register_4_q));  // open: clr
  Register #(.width(32)) register_5 (
    .D(WData), .en(demultiplexer_1_out4), .clk(Clock_in), .Q(register_5_q));  // open: clr
  Register #(.width(32)) register_6 (
    .D(WData), .en(demultiplexer_1_out5), .clk(Clock_in), .Q(register_6_q));  // open: clr
  Register #(.width(32)) register_7 (.D(WData), .en(demultiplexer_1_out6), .Q(register_7_q));  // open: clk, clr
  Register #(.width(32)) register_8 (
    .D(WData), .en(demultiplexer_1_out7), .clk(Clock_in), .Q(register_8_q));  // open: clr
  Register #(.width(32)) register_9 (
    .D(WData), .en(demultiplexer_1_out8), .clk(Clock_in), .Q(register_9_q));  // open: clr
  Register #(.width(32)) register_10 (
    .D(WData), .en(demultiplexer_1_out9), .clk(Clock_in), .Q(register_10_q));  // open: clr
  Register #(.width(32)) register_11 (
    .D(WData), .en(demultiplexer_1_out10), .clk(Clock_in), .Q(register_11_q));  // open: clr
  Register #(.width(32)) register_12 (
    .D(WData), .en(demultiplexer_1_out11), .clk(Clock_in), .Q(register_12_q));  // open: clr
  Register #(.width(32)) register_13 (
    .D(WData), .en(demultiplexer_1_out12), .clk(Clock_in), .Q(register_13_q));  // open: clr
  Register #(.width(32)) register_14 (
    .D(WData), .en(demultiplexer_1_out13), .clk(Clock_in), .Q(register_14_q));  // open: clr
  Register #(.width(32)) register_15 (
    .D(WData), .en(demultiplexer_1_out14), .clk(Clock_in), .Q(register_15_q));  // open: clr
  Register #(.width(32)) register_16 (
    .D(WData), .en(demultiplexer_1_out15), .clk(Clock_in), .Q(register_16_q));  // open: clr
  Register #(.width(32)) register_17 (
    .D(WData), .en(demultiplexer_1_out16), .clk(Clock_in), .Q(register_17_q));  // open: clr
  Register #(.width(32)) register_18 (
    .D(WData), .en(demultiplexer_1_out17), .clk(Clock_in), .Q(register_18_q));  // open: clr
  Register #(.width(32)) register_19 (
    .D(WData), .en(demultiplexer_1_out18), .clk(Clock_in), .Q(register_19_q));  // open: clr
  Register #(.width(32)) register_20 (
    .D(WData), .en(demultiplexer_1_out19), .clk(Clock_in), .Q(register_20_q));  // open: clr
  Register #(.width(32)) register_21 (
    .D(WData), .en(demultiplexer_1_out20), .clk(Clock_in), .Q(register_21_q));  // open: clr
  Register #(.width(32)) register_22 (
    .D(WData), .en(demultiplexer_1_out21), .clk(Clock_in), .Q(register_22_q));  // open: clr
  Register #(.width(32)) register_23 (
    .D(WData), .en(demultiplexer_1_out22), .clk(Clock_in), .Q(register_23_q));  // open: clr
  Register #(.width(32)) register_24 (
    .D(WData), .en(demultiplexer_1_out23), .clk(Clock_in), .Q(register_24_q));  // open: clr
  Register #(.width(32)) register_25 (
    .D(WData), .en(demultiplexer_1_out24), .clk(Clock_in), .Q(register_25_q));  // open: clr
  Register #(.width(32)) register_26 (
    .D(WData), .en(demultiplexer_1_out25), .clk(Clock_in), .Q(register_26_q));  // open: clr
  Register #(.width(32)) register_27 (
    .D(WData), .en(demultiplexer_1_out26), .clk(Clock_in), .Q(register_27_q));  // open: clr
  Register #(.width(32)) register_28 (
    .D(WData), .en(demultiplexer_1_out27), .clk(Clock_in), .Q(register_28_q));  // open: clr
  Register #(.width(32)) register_29 (
    .D(WData), .en(demultiplexer_1_out28), .clk(Clock_in), .Q(register_29_q));  // open: clr
  Register #(.width(32)) register_30 (
    .D(WData), .en(demultiplexer_1_out29), .clk(Clock_in), .Q(register_30_q));  // open: clr
  Register #(.width(32)) register_31 (
    .D(WData), .en(demultiplexer_1_out30), .clk(Clock_in), .Q(register_31_q));  // open: clr
  Register #(.width(32)) register_32 (
    .D(WData), .en(demultiplexer_1_out31), .clk(Clock_in), .Q(register_32_q));  // open: clr
  Multiplexer #(.enable("false"), .select(5), .width(32)) multiplexer_1 (
    .in0(register_1_q), .in1(register_2_q), .in2(register_3_q), .in3(register_4_q), .in4(register_5_q),
    .in5(register_6_q), .in6(register_7_q), .in7(register_8_q), .in8(register_9_q), .in9(register_10_q),
    .in10(register_11_q), .in11(register_12_q), .in12(register_13_q), .in13(register_14_q),
    .in14(register_15_q), .in15(register_16_q), .in16(register_17_q), .in17(register_18_q),
    .in18(register_19_q), .in19(register_20_q), .in20(register_21_q), .in21(register_22_q),
    .in22(register_23_q), .in23(register_24_q), .in24(register_25_q), .in25(register_26_q),
    .in26(register_27_q), .in27(register_28_q), .in28(register_29_q), .in29(register_30_q),
    .in30(register_31_q), .in31(register_32_q), .out(RData1), .sel(RReg1));
  Multiplexer #(.enable("false"), .select(5), .width(32)) multiplexer_2 (
    .in0(register_1_q), .in1(register_2_q), .in2(register_3_q), .in3(register_4_q), .in4(register_5_q),
    .in5(register_6_q), .in6(register_7_q), .in7(register_8_q), .in8(register_9_q), .in9(register_10_q),
    .in10(register_11_q), .in11(register_12_q), .in12(register_13_q), .in13(register_14_q),
    .in14(register_15_q), .in15(register_16_q), .in16(register_17_q), .in17(register_18_q),
    .in18(register_19_q), .in19(register_20_q), .in20(register_21_q), .in21(register_22_q),
    .in22(register_23_q), .in23(register_24_q), .in24(register_25_q), .in25(register_26_q),
    .in26(register_27_q), .in27(register_28_q), .in28(register_29_q), .in29(register_30_q),
    .in30(register_31_q), .in31(register_32_q), .out(RData2), .sel(RReg2));
endmodule
